// Logisim project memory.circ as structural Verilog: 1 circuit, main circuit main
module main (
  input  [7:0] Address,
  input  [7:0] Data_in,
  input  Store,
  output [7:0] Data_out
);

  RAM #(.bus("separate")) ram_1 (
    .addr(Address), .din(Data_in), .data(Data_out), .clk(Store));  // open: str, sel, ld, clr
endmodule
